# Fritzing sketch cansat (saved by Fritzing 0.9.3b)

parts:
  MCU1 = Raspberry Pi Zero  # not connected
  Part1 = Adafruit BME680 [part_number="Adafruit #3660"]
  Part2 = Adafruit Feather RP2040 [part_number="Adafruit #4884"]
  U1 = LIPO-2000mAh [package=lipo-2000]
  Part3 = APC220 with antenna
  Part4 = Adafruit PA1010D Mini GPS Module [part_number="Adafruit #4415"]
  MPU-1 = Adafruit MPU6050
  IC3 = DIP - 8 pins [chip_label=IC package="DIP (Dual Inline) [THT]"]
  IC4 = DIP - 8 pins [chip_label=IC package="DIP (Dual Inline) [THT]"]
  J1 = Piezo Speaker

nets:
  GND: Part1.GND, Part2.GND, U1.-, IC3.OUT
  VCC: Part1.VCC, Part2.+3V3, Part4.VCC, IC4.OUT
  N1: Part1.SDI/SDA, Part2.SDA, Part4.SDA
  N2: Part1.SCK/SCL, Part2.SCL, Part4.SCL
  N3: Part2.D25, MPU-1.SCL
  N4: Part2.D24, MPU-1.SDA
  N5: Part2.A3, Part3.TXD
  N6: Part2.A2, Part3.RXD
  N7: Part2.D5, J1.pin2
  N8: Part2.VBAT, U1.+
  N9: Part3.GND, IC3.IN1
  N10: Part3.VCC, Part3.EN, Part3.SET, IC4.IN5
  N11: Part4.GND, IC3.IN3
  N12: MPU-1.VCC, IC4.IN4
  N13: MPU-1.GND, IC3.IN2
  N14: IC3.IN4, J1.pin1

custom parts:
  Adafruit Feather RP2040: A new chip means a new Feather, and the Raspberry Pi RP2040 is no exception. When we saw this chip we thought "this chip is going to be awesome when we give it the Feather Treatment" and so we did! This Feather features the RP2040, and all niceties you know and love about Feather Measures 2.0" x 0.9" x 0.28" (50.8mm x 22.8mm x 7mm) without headers soldered in Light as a (large?) feather - 5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
  APC220 with antenna: Radio transceiver module for Arduino operating in the 418-455MHz band.
  Adafruit PA1010D Mini GPS Module: This miniature GPS breakout is only 1" x 1" (~ 25mm x 25mm) but houses a complete GPS/GNSS solution with both I2C and UART interfaces. There's even an antenna on top so it's plug and play! Support for GPS, GLONASS, GALILEO, QZSS -165 dBm sensitivity, up to 10 Hz updates Up to 210 PRN channels with 99 search channels and 33 simultaneous tracking channels 5V friendly design and only 30mA current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
  Adafruit MPU6050: The MPU-6050 is a popular six axis accelerometer and gyroscope (gyro) that has all the info you need on how things are shakin' and spinnin' . With six axes of sensing and 16-bit measurements, you'll have everything you need to give your robot friend an inner ear. This combination of gyroscopes and accelerometers is commonly referred to as an Inertial Measurement Unit or IMU. Not so long ago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
  DIP - 8 pins: A DIP stand-in part for whatever IC you want. With 8 pins on a 300mil dual inline package (DIP) footprint.
